# Fritzing sketch EnergyMonitorConfig,fzz (saved by Fritzing 0.9.2b)
breadboards: 1

parts:
  WeMos_D1_Mini1 = WeMos D1 Mini
  IC1 = ADS1115 16-bit ADC Breakout
  S1 = Pushbutton [package="[THT]"]
  R1 = Resistor [tolerance=±5% resistance=220 package=THT]
  R2 = Resistor [tolerance=±5% resistance=25 package=THT]

nets:
  3V3: WeMos_D1_Mini1.3V3, IC1.VDD
  N1: WeMos_D1_Mini1.D1, IC1.SCL
  N2: WeMos_D1_Mini1.D2, IC1.SDA
  N3: WeMos_D1_Mini1.D7, S1.Pin_1, S1.Pin_2, R1.Pin_1
  N4: WeMos_D1_Mini1.G, IC1.GND, R1.Pin_0
  N5: IC1.A0, R2.Pin_0
  N6: IC1.A1, R2.Pin_1
  N7: S1.Pin_3, S1.Pin_4

notes:
  to STC013 Current Sensor

custom parts:
  WeMos D1 Mini: The D1 mini is a mini wifi board based on ESP-8266EX.
  ADS1115 16-bit ADC Breakout: ADS1015 12-bit I2C ADC+PGA Breakout
